# Fritzing sketch layout (saved by Fritzing 0.9.3b)
breadboards: 1

parts:
  U1 = LM386 [package=dip08]
  IC1 = IC, DIP package, 14 pins [chip_label=CD40106]
  R1 = Photocell (LDR) [package=THT]
  VCC1 = Battery block 9V
  Part1 = Rotary Potentiometer [package=THT]
  100uF = Electrolytic Capacitor [capacitance=47µF package="100 mil [THT, electrolytic]"]
  0_01 = Capacitor [package=cap-pth-small2]
  J1 = Piezo Speaker
  0_22uF = Film/Foil Capacitor [capacitance=100nF voltage=35V package="5mm [THT, pp]"]
  D1 = Rectifier Diode [package="Melf DO-213 AA [SMD]"]  # not connected
  D2 = Rectifier Diode [package="Melf DO-213 AA [SMD]"]  # not connected
  D3 = Rectifier Diode [package="Melf DO-213 AA [SMD]"]  # not connected
  D4 = Rectifier Diode [package="Melf DO-213 AA [SMD]"]  # not connected
  0_22uF_2 = Film/Foil Capacitor [capacitance=100nF voltage=35V package="5mm [THT, pp]"]

nets:
  N1: U1.-IN, Part1.wiper, 0_01.2
  N2: U1.+IN, U1.V-, IC1.pin7, VCC1.-, Part1.leg2, 0_01.1, J1.pin2, 0_22uF.+, 0_22uF_2.-
  N3: U1.OUT, 100uF.+
  N4: U1.V+, IC1.pin14, VCC1.+, 0_22uF.-
  N5: IC1.pin5, R1.pin_0, 0_22uF_2.+
  N6: IC1.pin6, R1.pin_1, Part1.leg1
  N7: 100uF.-, J1.pin1

custom parts:
  Rotary Potentiometer: Rotary Potentiometer(16mm)
